# Fritzing sketch Spaduino (saved by Fritzing 0.9.3b)
breadboards: 1

parts:
  R1 = Resistor [tolerance=±5% resistance=10k package=THT]
  R2 = Resistor [tolerance=±5% resistance=6.8k package=THT]
  R3 = Resistor [tolerance=±5% resistance=6.8k package=THT]
  R4 = Resistor [tolerance=±5% resistance=1k package=THT]
  LED1 = LED - 3mm [color="Red (633nm)" package="3 mm [THT]"]
  C1 = Ceramic Capacitor [capacitance=100nF package="100 mil [THT, multilayer]"]
  C2 = Ceramic Capacitor [capacitance=100nF package="100 mil [THT, multilayer]"]
  C3 = Electrolytic Capacitor [capacitance=1µF package="100 mil [THT, electrolytic]"]
  R5 = Resistor [tolerance=±5% resistance=220 package=THT]
  U1 = atmega328 [package=dip]
  U2 = Voltage Regulator - 5V [package="TO220 [THT]"]

nets:
  N1: R1.Pin_0, R2.Pin_1, R3.Pin_1, C1.1, C2.1, C3.+, U1.VCC, U1.AVCC, U2.output_voltage
  N2: R1.Pin_1, U1.RESET
  N3: R2.Pin_0, U1.A5
  N4: R3.Pin_0, U1.A4
  N5: R4.Pin_0, U1.D11_(PWM)
  N6: R4.Pin_1, LED1.anode
  GND: LED1.cathode, C1.0, C2.0, C3.-, U1.GND, U2.GND
  N7: R5.Pin_1, U1.D4

notes:
  Pin 1
  Pin 4
  Pin 5
  Pin 6
  Pin 8
  SDA
  SCL
